# Fritzing sketch Projeto Arduíno Bluetooth,fotoresistor, servo motor, garagem (saved by Fritzing 0.9.10b)
breadboards: 2

parts:
  Componente1 = Bluetooth HC-05 Macho  # not connected
  Componente2 = Arduino Uno (Rev3)
  R1 = Resistor [tolerance=±5% power=0.25 resistance=2200 package=THT]
  R2 = Photocell (LDR) [package=THT]
  R3 = Resistor [tolerance=±5% power=0.25 resistance=1000 package=THT]
  LED1 = LED - 5mm [color="Red (633nm)" current=0.030 package="5 mm [THT]"]
  R4 = Resistor [tolerance=±5% power=0.25 resistance=330 package=THT]
  R5 = Resistor [tolerance=±5% power=0.25 resistance=1000 package=THT]
  LED2 = LED - 5mm [color="Red (633nm)" current=0.030 package="5 mm [THT]"]
  R6 = Resistor [tolerance=±5% power=0.25 resistance=330 package=THT]
  J1 = Basic Servo
  Componente3 = Arduino Uno (Rev3)
  SEN1 = US-100 Ultrasonic Distance Sensor
  LED3 = LED - 5mm [color="Red (633nm)" current=0.030 package="5 mm [THT]"]
  R7 = Resistor [tolerance=±5% power=0.25 resistance=330 package=THT]
  LED4 = LED - 5mm [color="Red (633nm)" current=0.030 package="5 mm [THT]"]
  R8 = Resistor [tolerance=±5% power=0.25 resistance=330 package=THT]
  LED5 = LED - 5mm [color="Red (633nm)" current=0.030 package="5 mm [THT]"]
  R9 = Resistor [tolerance=±5% power=0.25 resistance=330 package=THT]
  LED6 = LED - 5mm [color="Red (633nm)" current=0.030 package="5 mm [THT]"]
  R10 = Resistor [tolerance=±5% power=0.25 resistance=330 package=THT]
  J2 = Piezo Speaker

nets:
  N1: Componente2.A1, R2.pin_0, R5.Pin_1
  N2: Componente2.D11_PWM/MOSI, J1.pulse
  N3: Componente2.D12/MISO, LED1.anode
  N4: Componente2.D13/SCK, LED2.cathode
  N5: Componente2.D1/TX, R1.Pin_0
  5V: Componente2.5V, R2.pin_1, R3.Pin_1, J1.vcc
  N6: R1.Pin_1, R3.Pin_0
  N7: LED1.cathode, R4.Pin_1
  N8: R4.Pin_0, R5.Pin_0, R6.Pin_0, J1.gnd
  N9: LED2.anode, R6.Pin_1
  N10: Componente3.D8, R8.Pin_0
  N11: Componente3.D9_PWM, R7.Pin_0
  N12: Componente3.D11_PWM/MOSI, SEN1.TRIG
  N13: Componente3.D12/MISO, SEN1.ECHO
  N14: Componente3.D3_PWM, SEN1.VCC
  N15: Componente3.D6_PWM, R10.Pin_0
  N16: Componente3.D7, R9.Pin_0
  N17: SEN1.GND, SEN1.GND-2, LED3.cathode, LED4.cathode, LED5.cathode, LED6.cathode, J2.pin1
  N18: LED3.anode, R7.Pin_1
  N19: LED4.anode, R8.Pin_1
  N20: LED5.anode, R9.Pin_1
  N21: LED6.anode, R10.Pin_1
